// Logisim project BC16-V1.circ as structural Verilog: 9 circuits, main circuit bc-16
module bc_16 (
  input  [15:0] data_in,
  input  CLK,
  output suspended,
  output [15:0] data_out,
  output [15:0] address_bus,
  output enable_mem_writing
);

  wire and_1_out, div_op, enable_mem_writing_t, enable_mod, enable_reg_writing, not_1_out, not_2_out,
       not_3_out;
  wire [2:0] alu_func;
  wire [3:0] reg_0_add, reg_1_add, reg_writing_address;
  wire [15:0] arithmetic_logic_unit_1_result, current_instruction, mod, op_0, op_1, reg_0, reg_data_in;

  register_16 IR (.data_in(data_in), .enable_writing(CLK), .data_out(current_instruction));
  arithmetic_logic_unit arithmetic_logic_unit_1 (
    .op0(op_0), .op1(op_1), .func(alu_func), .result(arithmetic_logic_unit_1_result), .mod(mod),
    .div_op(div_op));
  control_unit control_unit_1 (
    .instruction_in(current_instruction), .data_in(data_in), .reg_0(reg_0), .reg_1(data_out),
    .alu_result(arithmetic_logic_unit_1_result), .reg_0_address(reg_0_add), .reg_1_address(reg_1_add),
    .writing_reg_address(reg_writing_address), .reg_data_out(reg_data_in), .mem_add(address_bus),
    .enable_mem_writing(enable_mem_writing_t), .enable_reg_writing(enable_reg_writing), .CLK(CLK),
    .cpu_suspended(suspended), .alu_func(alu_func), .op0(op_0), .op1(op_1));
  not not_1 (not_1_out, CLK);
  and and_1 (and_1_out, enable_reg_writing, not_1_out);
  register_file_16 register_file_16_1 (
    .data_in(reg_data_in), .writing_enabled(and_1_out), .writing_reg_address(reg_writing_address),
    .mod_in(mod), .mod_enabled(enable_mod), .reading_0_reg_address(reg_0_add),
    .reading_1_reg_address(reg_1_add), .data_out_0(reg_0), .data_out_1(data_out));
  not not_2 (not_2_out, CLK);
  and and_2 (enable_mod, div_op, not_3_out);
  not not_3 (not_3_out, CLK);
  and and_3 (enable_mem_writing, enable_mem_writing_t, not_2_out);

  // Other names for the same wires on the sheet: cpu_suspended = suspended; mem_address[15:0] = address_bus;
  //   mem_data_in[15:0] = data_in; reg_1[15:0] = data_out
endmodule

module register_16 (
  input  [15:0] data_in,
  input  enable_writing,
  output [15:0] data_out
);

  D_Flip_Flop b0 (.clk(enable_writing), .D(data_in[0]), .Q(data_out[0]));  // open: Qn, preset, en, reset
  D_Flip_Flop b1 (.clk(enable_writing), .D(data_in[1]), .Q(data_out[1]));  // open: Qn, preset, en, reset
  D_Flip_Flop b2 (.clk(enable_writing), .D(data_in[2]), .Q(data_out[2]));  // open: Qn, preset, en, reset
  D_Flip_Flop b3 (.clk(enable_writing), .D(data_in[3]), .Q(data_out[3]));  // open: Qn, preset, en, reset
  D_Flip_Flop b4 (.clk(enable_writing), .D(data_in[4]), .Q(data_out[4]));  // open: Qn, preset, en, reset
  D_Flip_Flop b5 (.clk(enable_writing), .D(data_in[5]), .Q(data_out[5]));  // open: Qn, preset, en, reset
  D_Flip_Flop b6 (.clk(enable_writing), .D(data_in[6]), .Q(data_out[6]));  // open: Qn, preset, en, reset
  D_Flip_Flop b7 (.clk(enable_writing), .D(data_in[7]), .Q(data_out[7]));  // open: Qn, preset, en, reset
  D_Flip_Flop b8 (.clk(enable_writing), .D(data_in[8]), .Q(data_out[8]));  // open: Qn, preset, en, reset
  D_Flip_Flop b9 (.clk(enable_writing), .D(data_in[9]), .Q(data_out[9]));  // open: Qn, preset, en, reset
  D_Flip_Flop b10 (.clk(enable_writing), .D(data_in[10]), .Q(data_out[10]));  // open: Qn, preset, en, reset
  D_Flip_Flop b11 (.clk(enable_writing), .D(data_in[11]), .Q(data_out[11]));  // open: Qn, preset, en, reset
  D_Flip_Flop b12 (.clk(enable_writing), .D(data_in[12]), .Q(data_out[12]));  // open: Qn, preset, en, reset
  D_Flip_Flop b13 (.clk(enable_writing), .D(data_in[13]), .Q(data_out[13]));  // open: Qn, preset, en, reset
  D_Flip_Flop b14 (.clk(enable_writing), .D(data_in[14]), .Q(data_out[14]));  // open: Qn, preset, en, reset
  D_Flip_Flop b15 (.clk(enable_writing), .D(data_in[15]), .Q(data_out[15]));  // open: Qn, preset, en, reset
endmodule

module register_file_16 (
  input  [15:0] data_in,
  input  [15:0] mod_in,
  input  mod_enabled,
  input  [3:0] reading_0_reg_address,
  input  writing_enabled,
  input  [3:0] reading_1_reg_address,
  input  [3:0] writing_reg_address,
  output [15:0] data_out_0,
  output [15:0] data_out_1
);

  wire and_1_out, and_2_out, and_3_out, and_4_out, and_5_out, and_6_out, and_7_out, and_8_out, and_9_out,
       and_10_out, decoder_1_out1, decoder_1_out2, decoder_1_out8, decoder_1_out9, decoder_1_out10,
       decoder_1_out11, decoder_1_out12, decoder_1_out13, decoder_1_out14, decoder_1_out15;
  wire [15:0] d1, d2, d3, d8, d9, da, db, dc, dd, de, df;

  Decoder #(.select(4), .enable("false")) decoder_1 (
    .out1(decoder_1_out1), .out2(decoder_1_out2), .out8(decoder_1_out8), .out9(decoder_1_out9),
    .out10(decoder_1_out10), .out11(decoder_1_out11), .out12(decoder_1_out12), .out13(decoder_1_out13),
    .out14(decoder_1_out14), .out15(decoder_1_out15), .sel(writing_reg_address));  // open: out0, out3, out4, out5, out6, out7
  register_16 acc (.data_in(data_in), .enable_writing(and_1_out), .data_out(d1));
  and and_1 (and_1_out, writing_enabled, decoder_1_out1);
  register_16 conde (.data_in(data_in), .enable_writing(and_2_out), .data_out(d2));
  and and_2 (and_2_out, writing_enabled, decoder_1_out2);
  register_16 mod (.data_in(mod_in), .enable_writing(mod_enabled), .data_out(d3));
  register_16 r0 (.data_in(data_in), .enable_writing(and_3_out), .data_out(d8));
  and and_3 (and_3_out, writing_enabled, decoder_1_out8);
  register_16 r1 (.data_in(data_in), .enable_writing(and_4_out), .data_out(d9));
  and and_4 (and_4_out, writing_enabled, decoder_1_out9);
  register_16 r2 (.data_in(data_in), .enable_writing(and_5_out), .data_out(da));
  and and_5 (and_5_out, writing_enabled, decoder_1_out10);
  register_16 r3 (.data_in(data_in), .enable_writing(and_6_out), .data_out(db));
  and and_6 (and_6_out, writing_enabled, decoder_1_out11);
  and and_7 (and_7_out, writing_enabled, decoder_1_out12);
  and and_8 (and_8_out, writing_enabled, decoder_1_out13);
  and and_9 (and_9_out, writing_enabled, decoder_1_out14);
  and and_10 (and_10_out, writing_enabled, decoder_1_out15);
  register_16 r4 (.data_in(data_in), .enable_writing(and_7_out), .data_out(dc));
  register_16 r5 (.data_in(data_in), .enable_writing(and_8_out), .data_out(dd));
  register_16 r6 (.data_in(data_in), .enable_writing(and_9_out), .data_out(de));
  register_16 r7 (.data_in(data_in), .enable_writing(and_10_out), .data_out(df));
  Multiplexer #(.select(4), .width(16), .enable("false")) multiplexer_1 (
    .in0({16{1'b0}}), .in1(d1), .in2(d2), .in3(d3), .in4(16'h1), .in5(16'h2), .in6(16'h4), .in7(16'hfff),
    .in8(d8), .in9(d9), .in10(da), .in11(db), .in12(dc), .in13(dd), .in14(de), .in15(df), .out(data_out_0),
    .sel(reading_0_reg_address));
  Multiplexer #(.select(4), .width(16), .enable("false")) multiplexer_2 (
    .in0({16{1'b0}}), .in1(d1), .in2(d2), .in3(d3), .in4(16'h1), .in5(16'h2), .in6(16'h4), .in7(16'hfff),
    .in8(d8), .in9(d9), .in10(da), .in11(db), .in12(dc), .in13(dd), .in14(de), .in15(df), .out(data_out_1),
    .sel(reading_1_reg_address));

  // Other names for the same wires on the sheet: mod[15:0] = mod_in; writing_enable = writing_enabled
endmodule

module control_unit (
  input  [15:0] instruction_in,
  input  [15:0] data_in,
  input  [15:0] reg_0,
  input  [15:0] reg_1,
  input  [15:0] alu_result,
  input  CLK,
  output [3:0] reg_0_address,
  output [3:0] reg_1_address,
  output [3:0] writing_reg_address,
  output [15:0] reg_data_out,
  output [15:0] mem_add,
  output enable_mem_writing,
  output enable_reg_writing,
  output [2:0] alu_func,
  output [15:0] op0,
  output [15:0] op1,
  output cpu_suspended
);

  wire bc, comparator_1_eq, enable_branch, halt, j, lw, not_1_out, not_2_out, or_1_out;
  wire [1:0] inst_type;
  wire [2:0] func;
  wire [3:0] s0, s1, s2;
  wire [7:0] field_selector_1_xxxx_octet;
  wire [11:0] shamt;
  wire [15:0] bit_extender_1_out, bit_extender_3_out, immediate, inst_fetch;

  Multiplexer #(.select(2), .width(4), .enable("false")) multiplexer_1 (
    .in0(4'b0010), .in1(s0), .in2(s1), .in3(s1), .out(reg_0_address), .sel(inst_type));
  Multiplexer #(.select(2), .width(16), .enable("false")) multiplexer_2 (
    .in0(reg_0), .in1(reg_0), .in2(reg_0), .in3(reg_0), .out(op0), .sel(inst_type));
  Multiplexer #(.select(2), .width(3), .enable("false")) multiplexer_3 (
    .in0(3'b100), .in1(alu_func), .in2(alu_func), .in3(alu_func), .out(func));  // open: sel
  instruction_decoder instruction_decoder_1 (
    .instruction_in(instruction_in), .inst_type(inst_type), .fields(shamt), .lw(lw), .sw(enable_mem_writing),
    .j(j), .halt(halt), .bc(bc), .func(alu_func));
  field_selector field_selector_1 (
    .fields(shamt), .quartet0(s0), .quartet1(s1), .quartet2(s2), .xxxx_octet(field_selector_1_xxxx_octet));
  assign bit_extender_1_out = {{12{1'b0}}, s2};  // Bit_Extender bit_extender_1
  Multiplexer #(.select(2), .width(16), .enable("false")) multiplexer_4 (
    .in0(reg_1), .in1(immediate), .in2(reg_1), .in3(bit_extender_1_out), .out(op1), .sel(inst_type));
  assign immediate = {{8{1'b0}}, field_selector_1_xxxx_octet};  // Bit_Extender bit_extender_2
  Multiplexer #(.select(2), .width(4), .enable("false")) multiplexer_5 (
    .in0(4'b0000), .in1(4'b0001), .in2(s2), .out(reg_1_address), .sel(inst_type));  // open: in3
  Multiplexer #(.select(2), .width(16), .enable("false")) multiplexer_6 (
    .in1(data_in), .in2(alu_result), .in3(alu_result), .out(reg_data_out), .sel(inst_type));  // open: in0
  assign bit_extender_3_out = {{4{1'b0}}, shamt};  // Bit_Extender bit_extender_3
  program_counter program_counter_1 (
    .shift_amount(bit_extender_3_out), .jump(bit_extender_3_out), .jump_flag(j), .branch_flag(enable_branch),
    .reset_flag(cpu_suspended), .instruction_fetch(inst_fetch), .CLK(CLK));
  Multiplexer #(.select(2), .width(4), .enable("false")) multiplexer_7 (
    .in1(4'b0001), .in2(s0), .in3(s0), .out(writing_reg_address), .sel(inst_type));  // open: in0
  not not_1 (not_1_out, CLK);
  or or_1 (or_1_out, halt, cpu_suspended);
  Multiplexer #(.width(16), .enable("false")) multiplexer_8 (
    .in0(inst_fetch), .in1(alu_result), .out(mem_add), .sel(CLK));
  D_Flip_Flop d_ff_1 (.clk(not_1_out), .D(or_1_out), .Q(cpu_suspended));  // open: Qn, preset, en, reset
  nor nor_1 (enable_reg_writing, enable_mem_writing, j, bc);
  Comparator #(.width(16)) comparator_1 (.a(reg_0), .b({16{1'b0}}), .eq(comparator_1_eq));  // open: gt, lt
  not not_2 (not_2_out, comparator_1_eq);
  and and_1 (enable_branch, not_2_out, bc);

  // Other names for the same wires on the sheet: mem_address[15:0] = mem_add; mem_data[15:0] = data_in;
  //   op_0[15:0] = op0; op_1[15:0] = op1; reading_reg_0_address[3:0] = reg_0_address;
  //   reading_reg_1_address[3:0] = reg_1_address; suspended = cpu_suspended; sw = enable_mem_writing
endmodule

module arithmetic_logic_unit (
  input  [15:0] op0,
  input  [15:0] op1,
  input  [2:0] func,
  output [15:0] result,
  output [15:0] mod,
  output div_op
);

  wire [2:0] comparison;
  wire [15:0] \and , multiplication, \not , \or , quocient, subtraction, sum;

  Adder #(.width(16)) adder_1 (.a(op0), .b(op1), .out(sum));  // open: cin, cout
  Subtractor #(.width(16)) subtractor_1 (.a(op0), .b(op1), .out(subtraction));  // open: bin, bout
  Multiplier #(.width(16)) multiplier_1 (.a(op0), .b(op1), .out(multiplication));  // open: cin, cout
  Divider #(.width(16)) divider_1 (.a(op0), .b(op1), .out(quocient), .rem(mod));  // open: upper
  Comparator #(.width(16)) comparator_1 (.a(op0), .b(op1), .gt(comparison[1]), .eq(comparison[0]), .lt(comparison[2]));
  assign \and  = op0 & op1;  // AND_Gate and_1, 16 bits wide
  assign \or  = op0 | op1;  // OR_Gate or_1, 16 bits wide
  assign \not  = ~op0;  // NOT_Gate not_1, 16 bits wide
  Multiplexer #(.select(3), .width(16), .enable("false")) multiplexer_1 (
    .in0(sum), .in1(multiplication), .in2(subtraction), .in3(quocient), .in4({{13{1'b0}}, comparison}),
    .in5(\and ), .in6(\or ), .in7(\not ), .out(result), .sel(func));
  Decoder #(.select(3), .enable("false")) decoder_1 (
    .out3(div_op), .sel(func));  // open: out0, out1, out2, out4, out5, out6, out7

  // Other names for the same wires on the sheet: eq = comparison[0]; gt = comparison[1]; lt = comparison[2];
  //   operand0[15:0] = op0; operand1[15:0] = op1
endmodule

module computer_sim (
);

  wire bc_16_1_suspended, CLOCK_out, enable_mem_writing;
  wire [15:0] mem_address, mem_writing_data, ram_1_data;

  RAM #(.addrWidth(16), .dataWidth(16), .bus("separate")) ram_1 (
    .addr(mem_address), .din(mem_writing_data), .data(ram_1_data), .str(enable_mem_writing),
    .clk(enable_mem_writing));  // open: sel, ld, clr
  Clock CLOCK (.out(CLOCK_out));
  LED CPU_SUSPENSION (.in(bc_16_1_suspended));
  bc_16 bc_16_1 (
    .data_in(ram_1_data), .suspended(bc_16_1_suspended), .CLK(CLOCK_out), .data_out(mem_writing_data),
    .address_bus(mem_address), .enable_mem_writing(enable_mem_writing));
endmodule

module instruction_decoder (
  input  [15:0] instruction_in,
  output [1:0] inst_type,
  output [11:0] fields,
  output [2:0] func,
  output lw,
  output sw,
  output j,
  output halt,
  output bc
);

  wire add, addg, addi, \and , cmp, div, inst_a, inst_b, inst_c, inst_d, logical, mult, multg, multi, \not ,
       \or , sub, subg, subi;
  wire [3:0] bitselector_1_out;

  or or_1 (inst_type[0], inst_b, inst_d);
  or or_2 (inst_type[1], inst_c, inst_d);
  or or_3 (inst_a, halt, j, bc);
  Decoder #(.select(4), .enable("false")) decoder_1 (
    .out0(halt), .out1(lw), .out2(sw), .out3(bc), .out4(j), .out5(add), .out6(addi), .out7(mult),
    .out8(multi), .out9(sub), .out10(subi), .out11(div), .out12(cmp), .out13(\and ), .out14(\or ),
    .out15(\not ), .sel(bitselector_1_out));
  BitSelector #(.width(16), .group(4)) bitselector_1 (.in(instruction_in), .out(bitselector_1_out), .sel(2'b11));
  or or_4 (inst_b, lw, sw);
  or or_5 (inst_c, logical, add, mult, sub, div, cmp);
  or or_6 (func[0], multg, div, \and , \not );
  or or_7 (func[1], subg, div, \or , \not );
  or or_8 (func[2], cmp, \or , \and , \not );
  or or_9 (addg, addi, add);
  or or_10 (multg, mult, multi);
  or or_11 (subg, sub, subi);
  or or_12 (logical, \not , \and , \or );
  or or_13 (inst_d, addi, subi, multi);

  assign fields = instruction_in[11:0];
endmodule

module program_counter (
  input  [15:0] shift_amount,
  input  [15:0] jump,
  input  jump_flag,
  input  CLK,
  input  branch_flag,
  input  reset_flag,
  output [15:0] instruction_fetch
);

  wire not_1_out;
  wire [15:0] adder_1_out, multiplexer_1_out, multiplexer_2_out, multiplexer_3_out;

  Multiplexer #(.width(16), .enable("false")) multiplexer_1 (
    .in0(multiplexer_2_out), .in1({16{1'b0}}), .out(multiplexer_1_out), .sel(reset_flag));
  Multiplexer #(.width(16), .enable("false")) multiplexer_2 (
    .in0(adder_1_out), .in1({instruction_fetch[15:12], jump[11:0]}), .out(multiplexer_2_out), .sel(jump_flag));
  register_16 PC (.data_in(multiplexer_1_out), .enable_writing(not_1_out), .data_out(instruction_fetch));
  not not_1 (not_1_out, CLK);
  Multiplexer #(.width(16), .enable("false")) multiplexer_3 (
    .in0({16{1'b0}}), .in1(shift_amount), .out(multiplexer_3_out), .sel(branch_flag));
  Adder #(.width(16)) adder_1 (
    .a(instruction_fetch), .b(multiplexer_3_out), .out(adder_1_out), .cin(1'b1));  // open: cout

  // Other names for the same wires on the sheet: b = branch_flag; inst_fetch[15:0] = instruction_fetch;
  //   j_pc[15:0] = {instruction_fetch[15:12], jump[11:0]}; j = jump_flag; reset = reset_flag;
  //   shamt[15:0] = shift_amount
endmodule

module field_selector (
  input  [11:0] fields,
  output [3:0] quartet0,
  output [3:0] quartet1,
  output [3:0] quartet2,
  output [7:0] xxxx_octet
);


  assign quartet0 = fields[11:8];
  assign quartet1 = fields[7:4];
  assign quartet2 = fields[3:0];
  assign xxxx_octet = fields[7:0];
endmodule
